# Fritzing sketch finradio-v0.0.2 (saved by Fritzing 0.9.9b)
breadboards: 1

parts:
  Mod1 = Raspberry Pi 4B
  RE1 = Rotary Encoder [package=THT]
  Grove1 = Grove OLED 128x96
  LED1 = LED - 3mm [color="Yellow (592nm)" current=0.030 package="3 mm [THT]"]
  LED2 = LED - 3mm [color="Green (560nm)" current=0.030 package="3 mm [THT]"]
  R1 = Resistor [tolerance=±5% resistance=220 package="0805 [SMD]"]
  R2 = Resistor [tolerance=±5% resistance=220 package="0805 [SMD]"]
  SP1 = SPEAKER [package=pcb_mount_speaker]  # not connected
  RE2 = Rotary Encoder [package=THT]
  ENCODER1 = Rotary Encoder with Knob  # not connected

nets:
  3V3: Mod1.3V3, RE1.EncoderPinB, Grove1.VCC, RE2.EncoderPinB
  N1: Mod1.GPIO2, Grove1.SDA
  N2: Mod1.GPIO3, Grove1.SCL
  GND: Mod1.GND, Grove1.GND, LED1.cathode, LED2.cathode
  N3: Mod1.GPIO27, RE1.EncoderPinA
  N4: Mod1.GPIO22, RE1.EncoderPinC
  N5: Mod1.GPIO5, RE2.EncoderPinA
  N6: Mod1.GPIO6, LED1.anode, R1.Pin_0, R1.Pin_1
  N7: Mod1.GPIO16, RE2.EncoderPinC
  N8: Mod1.GPIO26, LED2.anode, R2.Pin_0, R2.Pin_1

notes:
  0.96", 128x64, SSD1306
  Tune up feedback
  Tune down feedback
  Tuning knob
  Volume
  knob

custom parts:
  Rotary Encoder with Knob: Rotary Encoder with 1/4" Shaft and Knob
